# Fritzing sketch BiColourLED (saved by Fritzing 0.9.4)
breadboards: 1

parts:
  Arduino_Uno = Arduino Uno (Rev3)
  R1 = Resistor [tolerance=±5% resistance=220 package=THT]
  R2 = Resistor [tolerance=±5% resistance=220 package=THT]
  R3 = Resistor [tolerance=±5% resistance=470 package=THT]
  LED1 = LED - 5mm [color="Blue (470nm)" package="5 mm [THT]"]

nets:
  N1: Arduino_Uno.A0, R1.Pin_1, R2.Pin_0
  N2: Arduino_Uno.D8, LED1.anode
  N3: Arduino_Uno.GND, R1.Pin_0
  N4: Arduino_Uno.D7, R3.Pin_0
  N5: Arduino_Uno.5V, R2.Pin_1
  N6: R3.Pin_1, LED1.cathode
